# Fritzing sketch SAM_PI Wiring layout (saved by Fritzing 0.9.3b)
breadboards: 1

parts:
  LCD1 = LCD screen
  TR1 = Trimmer Potentiometer [package=THT]
  NFC_reader = RFID-RC522 Reader
  Raspberry_Pi_2 = Raspberry Pi 3 [part_number=RPI-3-V1.2]
  RED_LED = LED - 5mm [color="Red (633nm)" package="5 mm [THT]"]
  GREEN_LED = LED - 5mm [color="Green (555nm)" package="5 mm [THT]"]
  R2 = Resistor [tolerance=±1% resistance=68 package=THT]
  R3 = Resistor [tolerance=±1% resistance=68 package=THT]
  Fingerprint_USB_part = PowerBoost 500 Charger
  Fingerprint = FTDI Basic Programmer

nets:
  GND: LCD1.VSS, LCD1.R/W, LCD1.LED-, TR1.leg2, NFC_reader.GND, Raspberry_Pi_2.GND, RED_LED.cathode, GREEN_LED.cathode
  VDD: LCD1.VDD, LCD1.LED+, TR1.leg1, Raspberry_Pi_2.5V, Fingerprint_USB_part.USB
  N1: LCD1.V0, TR1.wiper
  N2: LCD1.RS, Raspberry_Pi_2.GPIO2
  N3: LCD1.E, Raspberry_Pi_2.GPIO3
  N4: LCD1.DB4, Raspberry_Pi_2.GPIO4
  N5: LCD1.DB5, Raspberry_Pi_2.GPIO17
  N6: LCD1.DB6, Raspberry_Pi_2.GPIO27
  N7: LCD1.DB7, Raspberry_Pi_2.GPIO22
  3.3V: NFC_reader.3.3V, Raspberry_Pi_2.3V3
  N8: NFC_reader.RST, Raspberry_Pi_2.GPIO25
  N9: NFC_reader.IRQ, NFC_reader.MISO, Raspberry_Pi_2.GPIO9
  N10: NFC_reader.MOSI, Raspberry_Pi_2.GPIO10
  N11: NFC_reader.SCK, Raspberry_Pi_2.GPIO11
  N12: NFC_reader.SDA, Raspberry_Pi_2.GPIO8
  N13: Raspberry_Pi_2.GPIO26, Raspberry_Pi_2.GPIO20, R2.Pin_1
  N14: Raspberry_Pi_2.GPIO21, R3.Pin_1
  N15: RED_LED.anode, R3.Pin_0
  N16: GREEN_LED.anode, R2.Pin_0
  N17: Fingerprint_USB_part.ENABLE, Fingerprint.CTS
  N18: Fingerprint_USB_part.LBO, Fingerprint.TXO
  GND_2: Fingerprint_USB_part.GND, Fingerprint.RXI, Fingerprint.GND
  N19: Fingerprint_USB_part.5.0V, Fingerprint.DTR
